# Fritzing sketch SQR_FG_ケース内配線 (saved by Fritzing 0.9.2b)
perfboards: 2

parts:
  J1 = female pin header, 3 pins [form="♀ (female)"]
  J2 = female pin header, 4 pins [form="♀ (female)"]
  J3 = female pin header, 4 pins [form="♀ (female)"]
  J4 = female pin header, 2 pins [form="♀ (female)"]
  J5 = female pin header, 2 pins [form="♀ (female)"]
  J7 = female pin header, 3 pins [form="♀ (female)"]
  J8 = female pin header, 3 pins [form="♀ (female)"]
  J9 = female pin header, 2 pins [form="♀ (female)"]
  RE1 = Rotary Encoder [package=THT]
  S1 = Pushbutton [package=THT]
  R1 = Rotary Potentiometer (Small) [maximum_resistance=100kΩ package=THT]
  VCC1 = Battery block 9V
  S2 = Toggle Switch [package=THT]
  R2 = Rotary Potentiometer (Small) [maximum_resistance=100kΩ package=THT]
  J6 = female pin header, 3 pins [form="♀ (female)"]
  TRS1 = Audio Jack (TRS) 3.5mm [package="4Ucon 08780 [THT]"]

nets:
  N1: J1.pin1, R1.leg1
  N2: J1.pin2, R1.wiper
  N3: J1.pin3, R1.leg2
  N4: J2.pin1, RE1.EncoderPinB
  N5: J2.pin2, RE1.EncoderPinC
  N6: J2.pin3, S1.leg0
  N7: J2.pin4, RE1.EncoderPinA, S1.leg1
  N8: J3.pin2, J8.pin3
  N9: J3.pin3, J8.pin2
  N10: J3.pin4, J8.pin1
  N11: J4.pin1, S2.COM
  N12: J4.pin2, VCC1.-
  N13: J5.pin1, J9.pin2
  N14: J5.pin2, J9.pin1
  N15: J7.pin1, R2.leg2
  N16: J7.pin2, R2.wiper
  N17: J7.pin3, R2.leg1
  N18: J6.pin1, TRS1.Ring
  N19: J6.pin2, TRS1.Sleeve
